// Logisim project lab 7.circ as structural Verilog: 6 circuits, main circuit main
module main (
  input  Cin,
  input  Ainvert,
  input  [1:0] Select,
  input  A,
  input  Binvert,
  input  B,
  input  Less,
  output Result,
  output CarryOut,
  output Set
);

  wire and_1_out, multiplexer_1_out, multiplexer_2_out, not_1_out, not_2_out, or_1_out;

  Multiplexer multiplexer_1 (.in0(A), .in1(not_1_out), .out(multiplexer_1_out), .sel(Ainvert));  // open: en
  not not_1 (not_1_out, A);
  Multiplexer multiplexer_2 (.in0(B), .in1(not_2_out), .out(multiplexer_2_out), .sel(Binvert));  // open: en
  not not_2 (not_2_out, B);
  and and_1 (and_1_out, multiplexer_1_out, multiplexer_2_out);
  or or_1 (or_1_out, multiplexer_1_out, multiplexer_2_out);
  Full_Adder full_adder_1 (
    .A(multiplexer_1_out), .B(multiplexer_2_out), .Cin(Cin), .Cout(CarryOut), .Sum(Set));  // open: xor
  multiplexer multiplexer_3 (.A(and_1_out), .B(or_1_out), .C(Set), .D(Less), .Select(Select), .out_6(Result));
endmodule

module DLatch (
  input  D,
  input  clk,
  output Q,
  output Q_prime
);

  wire nand_1_out, nand_2_out;

  nand nand_1 (nand_1_out, D, D, clk);
  nand nand_2 (nand_2_out, clk, nand_1_out);
  nand nand_3 (Q, nand_1_out, Q_prime);
  nand nand_4 (Q_prime, Q, nand_2_out);
endmodule

module multiplexer (
  input  [1:0] Select,
  input  A,
  input  B,
  input  C,
  input  D,
  output out_6
);

  wire and_1_out, and_2_out, and_3_out, and_4_out, not_1_out, not_2_out;

  not not_1 (not_1_out, Select[0]);
  not not_2 (not_2_out, Select[1]);
  and and_1 (and_1_out, A, not_1_out, not_2_out);
  and and_2 (and_2_out, B, Select[0], not_2_out);
  and and_3 (and_3_out, C, not_1_out, Select[1]);
  and and_4 (and_4_out, D, Select[0], Select[1]);
  or or_1 (out_6, and_1_out, and_2_out, and_3_out, and_4_out);
endmodule

module half_adder (
  input  A,
  input  B,
  output Sum,
  output CarryOut
);

  xor xor_1 (Sum, A, B);
  and and_1 (CarryOut, B, A);
endmodule

module Full_Adder (
  input  Cin,
  input  A,
  input  B,
  output Sum,
  output \xor ,
  output Cout
);

  wire half_adder_1_carryout, half_adder_2_carryout;

  half_adder half_adder_1 (.A(A), .B(B), .Sum(\xor ), .CarryOut(half_adder_1_carryout));
  or or_1 (Cout, half_adder_1_carryout, half_adder_2_carryout);
  half_adder half_adder_2 (.A(Cin), .B(\xor ), .Sum(Sum), .CarryOut(half_adder_2_carryout));
endmodule

module _8bitALU (
  input  [1:0] Select,
  input  Ainvert,
  input  BNegate,
  input  [7:0] A,
  input  [7:0] B,
  output Zero,
  output [7:0] Output,
  output Overflow
);

  wire main_1_carryout, main_2_carryout, main_3_carryout, main_4_carryout, main_5_carryout, main_6_carryout,
       main_7_carryout, main_8_carryout, main_8_set;

  main main_1 (
    .Ainvert(Ainvert), .A(A[0]), .Binvert(A[6]), .B(B[0]), .Less(main_8_set), .Cin(A[6]), .Select(Select),
    .CarryOut(main_1_carryout), .Result(Output[0]));  // open: Set
  main main_2 (
    .Ainvert(Ainvert), .A(A[1]), .Binvert(A[6]), .B(B[1]), .Less(1'b0), .Cin(main_1_carryout),
    .Select(Select), .CarryOut(main_2_carryout), .Result(Output[1]));  // open: Set
  main main_3 (
    .Ainvert(Ainvert), .A(A[2]), .Binvert(A[6]), .B(B[2]), .Less(1'b0), .Cin(main_2_carryout),
    .Select(Select), .CarryOut(main_3_carryout), .Result(Output[2]));  // open: Set
  main main_4 (
    .Ainvert(Ainvert), .A(A[3]), .Binvert(A[6]), .B(B[3]), .Less(1'b0), .Cin(main_3_carryout),
    .Select(Select), .CarryOut(main_4_carryout), .Result(Output[3]));  // open: Set
  main main_5 (
    .Ainvert(Ainvert), .A(A[4]), .Binvert(A[6]), .B(B[4]), .Less(1'b0), .Cin(main_4_carryout),
    .Select(Select), .CarryOut(main_5_carryout), .Result(Output[4]));  // open: Set
  main main_6 (
    .Ainvert(Ainvert), .A(A[5]), .Binvert(A[6]), .B(B[5]), .Less(1'b0), .Cin(main_5_carryout),
    .Select(Select), .CarryOut(main_6_carryout), .Result(Output[5]));  // open: Set
  main main_7 (
    .Ainvert(Ainvert), .A(A[6]), .Binvert(A[6]), .B(B[6]), .Less(1'b0), .Cin(main_6_carryout),
    .Select(Select), .CarryOut(main_7_carryout), .Result(Output[6]));  // open: Set
  main main_8 (
    .Ainvert(Ainvert), .A(A[7]), .Binvert(A[6]), .B(B[7]), .Less(1'b0), .Cin(main_7_carryout),
    .Select(Select), .CarryOut(main_8_carryout), .Result(Output[7]), .Set(main_8_set));
  and and_1 (Overflow, main_7_carryout, main_8_carryout);
  nor nor_1 (Zero, Output[0], Output[1], Output[2], Output[3], Output[4], Output[5], Output[6], Output[7]);

  assign BNegate = A[6];

  // Notes on the sheet:
  //   Boone Tison
endmodule
